# Fritzing sketch Autotant (saved by Fritzing 0.9.3b)

parts:
  L298N2 = L298N DC motor driver
  L298N3 = L298N DC motor driver
  Parça1 = Bluetooth HC-05 Macho
  motor_RF = DC Motor
  motor_RB = DC Motor
  motor_LB = DC Motor
  Parça2 = Arduino Uno (Rev3) - ICSP
  motor_LF = DC Motor
  R1 = Resistor [tolerance=±5% resistance=1k package="0805 [SMD]"]
  R2 = Resistor [tolerance=±5% resistance=2.2k package="0603 [SMD]"]
  VCC1 = Battery

nets:
  N1: L298N2.OUT1, motor_RF.pin_2
  N2: L298N2.OUT2, motor_RF.pin_1
  N3: L298N2.OUT3, motor_LF.pin_2
  N4: L298N2.OUT4, motor_LF.pin_1
  N5: L298N2.ENA, Parça2.D6_PWM
  N6: L298N2.ENB, Parça2.D3_PWM
  N7: L298N2.IN1, Parça2.D7
  N8: L298N2.IN2, Parça2.D5_PWM
  N9: L298N2.IN3, Parça2.D2
  N10: L298N2.IN4, Parça2.D4
  N11: L298N3.OUT1, motor_LB.pin_2
  N12: L298N3.OUT2, motor_LB.pin_1
  N13: L298N3.OUT3, motor_RB.pin_2
  N14: L298N3.OUT4, motor_RB.pin_1
  N15: L298N3.12V, VCC1.+
  N16: L298N3.GND, VCC1.-
  N17: L298N3.ENA, Parça2.D10_PWM/SS
  N18: L298N3.ENB, Parça2.D13/SCK
  N19: L298N3.IN1, Parça2.D8
  N20: L298N3.IN2, Parça2.D9_PWM
  N21: L298N3.IN3, Parça2.D11_PWM/MOSI
  N22: L298N3.IN4, Parça2.D12/MISO
  N23: Parça1.TXD, Parça2.D0/RX
  N24: Parça1.RXD, R2.Pin_1
  VCC: Parça1.VCC, Parça2.5V
  GND: Parça1.GND, Parça2.GND, R2.Pin_0
  N25: Parça2.D1/TX, R1.Pin_1

custom parts:
  L298N DC motor driver: 2x DC motor driver with 78M05 positive voltage regulator (7..35 V) L298N: max 46 V, 2 A Set 5 V Enable jumper to enable 5 V regultor (needed for the L298N) and +5 V output at screw terminal or supply external +5 V at screw terminal Set ENA and/or ENB to +5 V to enable motor permanently or supply ENA and/or ENB with PWM signal IN1 and IN2 set rotation directory for motor A (OUT1/OUT2) IN2 and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
  Battery: Your standard 2x 18650 battery pack (7,4 Volts)
